# Fritzing sketch blinker-led-esterno (saved by Fritzing 1.0.4)
breadboards: 1

parts:
  Componente1 = Arduino Uno (Rev3) - ICSP
  LED1 = LED - 5mm [color="Red (633nm)" current=0.030A package="5 mm [THT]"]
  R1 = Resistor [tolerance=±5% resistance=220 package="2010 [SMD]"]

nets:
  N1: Componente1.GND, LED1.cathode
  N2: Componente1.D7, R1.Pin_1
  N3: LED1.anode, R1.Pin_0
